# Fritzing sketch FC - Fritzing Design (saved by Fritzing 0.9.3b)
circuit board: 16.2827cm x 9.38379cm

parts:
  Enable = RELAY [package=relay-t9a-2]
  Mode = RELAY [package=relay-t9a-2]
  Driver = SWITCH-MOMENTARY-2 [package=tactile-pth-12mm]
  U6 = RJ45 Jack [package=rj45-8]
  Stop = SWITCH-MOMENTARY-2 [package=tactile-pth-12mm]
  U5 = RJ45 Jack [package=rj45-8]
  Raspberry_Pi_1 = Raspberry Pi 3 [part_number=RPI-3-V1.2]
  SA = SWITCH-MOMENTARY-2 [package=tactile-pth-12mm]
  SD = SWITCH-MOMENTARY-2 [package=tactile-pth-12mm]
  Auto = SWITCH-MOMENTARY-2 [package=tactile-pth-12mm]

nets:
  N1: Enable.COIL1, Raspberry_Pi_1.GPIO27, Raspberry_Pi_1.GPIO22
  N2: Enable.COIL2, Mode.COIL1, Driver.2, U6.3, Stop.2, U5.3, Raspberry_Pi_1.GND, Raspberry_Pi_1.GPIO16, Raspberry_Pi_1.GPIO25, SA.2, SD.2, Auto.2
  N3: Enable.MAIN, U6.5, U5.5
  N4: Enable.NC, U6.6, U5.6
  N5: Mode.COIL2, Raspberry_Pi_1.GPIO17
  N6: Mode.MAIN, U6.1, U5.1
  N7: Mode.NO, U6.2, U5.2
  N8: Driver.1, Raspberry_Pi_1.GPIO5, Raspberry_Pi_1.GPIO6
  N9: U6.4, Raspberry_Pi_1.GPIO2
  N10: Stop.1, Raspberry_Pi_1.GPIO12
  N11: U5.4, Raspberry_Pi_1.3v3
  N12: Raspberry_Pi_1.GPIO19, SA.1
  N13: Raspberry_Pi_1.GPIO26, SD.1
  N14: Raspberry_Pi_1.GPIO24, Auto.1
